# Fritzing sketch PiNodeVsCodeSimpleCircuit (saved by Fritzing 0.9.3b)
breadboards: 1

parts:
  Raspberry_Pi_1 = Raspberry Pi 3 [part_number=RPI-3-V1.2]
  S1 = Momentary Switch [package=ksa_sealed_tac_switch]
  LED1 = smd LED [color="Green (560nm)" package="0805 [SMD]"]
  R1 = Resistor [tolerance=±5% resistance=330 package="1206 [SMD]"]

nets:
  N1: Raspberry_Pi_1.3v3, S1.2, S1.4
  N2: Raspberry_Pi_1.GIPO5, LED1.anode
  N3: Raspberry_Pi_1.GIPO6, S1.1, S1.3
  N4: Raspberry_Pi_1.GND, R1.Pin_1
  N5: LED1.cathode, R1.Pin_0
